// Logisim project Cache.circ as structural Verilog: 11 circuits, main circuit main
module main (
  input  EnableTestHalting,
  output [9:0] CorrectCounter,
  output [9:0] HitCounter,
  output [9:0] MissCounter,
  output [9:0] TestNumber,
  output [7:0] ByteRead,
  output [7:0] CorrectByteRead,
  output Halt
);

  wire and_3_out, and_4_out, and_5_out, CLK, CmdIsRead, Correct, CpuRead, CpuWrite, DidContain, HaltTesting,
       MaxItersReached, MemRead, MemWrite, not_1_out, not_2_out, not_4_out, NotDoneTesting, Ok2Count,
       or_1_out, Ready;
  wire [7:0] CpuWriteValue, MemAddress;
  wire [9:0] CpuAddress;
  wire [31:0] Line2Mem, LineFromMem;

  not not_1 (not_1_out, Ready);
  Clock clock_1 (.out(CLK));
  or or_1 (or_1_out, MaxItersReached, Ready);
  Counter #(.width(4), .max('h9)) MaxClocks (
    .load(Ready), .D(4'b0001), .count(not_1_out), .carry(MaxItersReached), .clk(CLK));  // open: Q, clr
  and and_1 (HaltTesting, EnableTestHalting, CmdIsRead, not_2_out);
  not not_2 (not_2_out, Correct);
  not not_3 (NotDoneTesting, Halt);
  Inputs inputs_1 (
    .HaltTesting(HaltTesting), .Ready(or_1_out), .CLK(CLK), .Done(Halt), .Read(CpuRead), .Write(CpuWrite),
    .Address(CpuAddress), .Value(CpuWriteValue), .TestNumber(TestNumber));
  Cache cache_1 (
    .CpuAddress(CpuAddress), .CpuRead(CpuRead), .CpuWrite(CpuWrite), .CpuWriteValue(CpuWriteValue),
    .CLK(CLK), .LineFromMem(LineFromMem), .Ready(Ready), .DidContain(DidContain), .ByteRead(ByteRead),
    .MemAddress(MemAddress), .MemRead(MemRead), .MemWrite(MemWrite), .Line2Mem(Line2Mem));
  // Probe on CpuRead
  // Probe on CpuWrite
  // Probe on CpuWriteValue
  // Probe on CpuAddress
  // Probe on CpuAddress
  // Probe on TestNumber
  // Probe on CorrectByteRead
  // Probe on Correct
  // Probe on Ready
  // Probe on DidContain
  // Probe on ByteRead
  // Probe on MemAddress
  // Probe on MemRead
  // Probe on MemWrite
  // Probe on HitCounter
  // Probe on LineFromMem
  // Probe on Line2Mem
  not not_4 (not_4_out, HaltTesting);
  RAM #(.dataWidth(32), .bus("separate")) ram_1 (
    .addr(MemAddress), .din(Line2Mem), .data(LineFromMem), .str(MemWrite), .clk(CLK), .ld(MemRead));  // open: sel, clr
  and and_2 (Ok2Count, Ready, not_4_out, NotDoneTesting);
  and and_3 (and_3_out, Correct, Ok2Count);
  and and_4 (and_4_out, DidContain, Ok2Count);
  and and_5 (and_5_out, MemRead, NotDoneTesting);
  Checker checker_1 (
    .TestNumber(TestNumber), .YourByteRead(ByteRead), .CmdIsRead(CmdIsRead),
    .CorrectByteRead(CorrectByteRead), .Correct(Correct));
  Counter #(.width(10), .max('h3ff)) u_CorrectCounter (
    .count(and_3_out), .Q(CorrectCounter), .clk(CLK));  // open: load, D, carry, clr
  Counter #(.width(10), .max('h3ff)) u_HitCounter (
    .count(and_4_out), .Q(HitCounter), .clk(CLK));  // open: load, D, carry, clr
  Counter #(.width(10), .max('h3ff)) u_MissCounter (
    .count(and_5_out), .Q(MissCounter), .clk(CLK));  // open: load, D, carry, clr
  // Probe on CorrectCounter
  // Probe on HitCounter
  // Probe on MissCounter

  // Other names for the same wires on the sheet: DoneTesting = Halt

  // Notes on the sheet:
  //   Your Answer Inside Here
endmodule

module Cache (
  input  [9:0] CpuAddress,
  input  CpuRead,
  input  CpuWrite,
  input  [7:0] CpuWriteValue,
  input  CLK,
  input  [31:0] LineFromMem,
  output Ready,
  output DidContain,
  output [7:0] ByteRead,
  output [7:0] MemAddress,
  output MemRead,
  output MemWrite,
  output [31:0] Line2Mem
);

  wire DidContain0, DidContain1, MemRead0, MemRead1, MemWrite0, MemWrite1, Read, Set0, Set1, Write;
  wire [1:0] BlockSize;
  wire [6:0] Tag;
  wire [7:0] ByteRead0, ByteRead1, MemAdress0, WriteValue;
  wire [7:1] MemAdress1;
  wire [31:0] Line2Mem0, Line2Mem1;

  Register #(.width(10)) State (
    .D(CpuAddress), .en(Ready), .Q({Tag, MemAdress0[0], BlockSize}), .clk(CLK));  // open: clr
  Register State_2 (.D(CpuWriteValue), .en(Ready), .Q(WriteValue), .clk(CLK));  // open: clr
  Register #(.width(1)) State_3 (.D(CpuRead), .en(Ready), .Q(Read), .clk(CLK));  // open: clr
  Register #(.width(1)) State_4 (.D(CpuWrite), .en(Ready), .Q(Write), .clk(CLK));  // open: clr
  StageSwitcher stageswitcher_1 (
    .CLK(CLK), .Ready(Ready));  // open: Stage1PrepareEvictSelect, Stage2WrtToMem, Stage3ReadFrmMem, Stage4WriteToCache, Stage5ReadfromCache, Stag6UpdateAges
  Multiplexer #(.enable("false")) multiplexer_1 (.in0(1'b1), .in1(1'b0), .out(Set0), .sel(MemAdress0[0]));
  Multiplexer #(.enable("false")) multiplexer_2 (.in0(1'b0), .in1(1'b1), .out(Set1), .sel(MemAdress0[0]));
  Set u_Set0 (
    .ThisSet(Set0), .CLK(CLK), .BlockSize(BlockSize), .Tag(Tag), .CpuRead(Read), .CpuWrite(Write),
    .CpuWriteValue(WriteValue), .LineFromMem(LineFromMem), .DidContain(DidContain0), .ByteRead(ByteRead0),
    .Tag_2(MemAdress0[7:1]), .MemRead(MemRead0), .MemWrite(MemWrite0), .Line2Mem(Line2Mem0));
  Set u_Set1 (
    .ThisSet(Set1), .CLK(CLK), .BlockSize(BlockSize), .Tag(Tag), .CpuRead(Read), .CpuWrite(Write),
    .CpuWriteValue(WriteValue), .LineFromMem(LineFromMem), .DidContain(DidContain1), .ByteRead(ByteRead1),
    .Tag_2(MemAdress1), .MemRead(MemRead1), .MemWrite(MemWrite1), .Line2Mem(Line2Mem1));
  Multiplexer #(.enable("false")) multiplexer_3 (
    .in0(DidContain0), .in1(DidContain1), .out(DidContain), .sel(MemAdress0[0]));
  Multiplexer #(.width(8), .enable("false")) multiplexer_4 (
    .in0(ByteRead0), .in1(ByteRead1), .out(ByteRead), .sel(MemAdress0[0]));
  Multiplexer #(.width(8), .enable("false")) multiplexer_5 (
    .in0(MemAdress0), .in1({MemAdress1, MemAdress0[0]}), .out(MemAddress), .sel(MemAdress0[0]));
  Multiplexer #(.enable("false")) multiplexer_6 (.in0(MemRead0), .in1(MemRead1), .out(MemRead), .sel(MemAdress0[0]));
  Multiplexer #(.enable("false")) multiplexer_7 (.in0(MemWrite0), .in1(MemWrite1), .out(MemWrite), .sel(MemAdress0[0]));
  Multiplexer #(.width(32), .enable("false")) multiplexer_8 (
    .in0(Line2Mem0), .in1(Line2Mem1), .out(Line2Mem), .sel(MemAdress0[0]));

  // Other names for the same wires on the sheet: MemAdress1[0] = MemAdress0[0]; SetBit = MemAdress0[0]

  // Notes on the sheet:
  //   Address Bits = 10
  //   Line Size = 4
  //   W = 3
  //   Num Sets = 2
  //   C =4*3*2 = 24bytes
endmodule

module Set (
  input  ThisSet,
  input  CLK,
  input  [1:0] BlockSize,
  input  [6:0] Tag,
  input  CpuRead,
  input  CpuWrite,
  input  [7:0] CpuWriteValue,
  input  [31:0] LineFromMem,
  output DidContain,
  output [7:0] ByteRead,
  output [6:0] Tag_2,
  output MemRead,
  output MemWrite,
  output [31:0] Line2Mem
);

  wire and_4_out, and_5_out, and_6_out, and_7_out, and_8_out, Dirty0, Dirty1, Dirty2, E0, E1, E2, Evict,
       MemRead0, MemRead1, MemRead2, MemWrite0, MemWrite1, MemWrite2, multiplexer_1_out, multiplexer_2_out,
       multiplexer_3_out, or_1_out, Ready, Select0, Select1, Select2, selectline_1_checkage,
       selectline_1_evict, Stage1, UpdateAge, Valid0, Valid1, Valid2;
  wire [1:0] Age0, Age1, Age2, evictduetoage_1_select, multiplexer_4_out, multiplexer_5_out,
       multiplexer_6_out, multiplexer_7_out, NewAge0, NewAge1, NewAge2, Select, selectline_1_choosebit0;
  wire [6:0] Tag0, Tag1, Tag2;
  wire [7:0] ByteRead0, ByteRead1, ByteRead2;
  wire [31:0] Line2Mem0, Line2Mem1, Line2Mem2;

  Multiplexer #(.select(2), .enable("false")) multiplexer_1 (
    .in0(1'b1), .in1(1'b0), .in2(1'b0), .in3(1'b0), .out(multiplexer_1_out), .sel(Select));
  Multiplexer #(.select(2), .enable("false")) multiplexer_2 (
    .in0(1'b0), .in1(1'b1), .in2(1'b0), .in3(1'b0), .out(multiplexer_2_out), .sel(Select));
  Multiplexer #(.select(2), .enable("false")) multiplexer_3 (
    .in0(1'b0), .in1(1'b0), .in2(1'b1), .in3(1'b0), .out(multiplexer_3_out), .sel(Select));
  and and_1 (Select0, multiplexer_1_out, ThisSet);
  and and_2 (Select1, multiplexer_2_out, ThisSet);
  and and_3 (Select2, multiplexer_3_out, ThisSet);
  Comparator #(.width(7), .mode("unsigned")) comparator_1 (.a(Tag), .b(Tag0), .eq(E0));  // open: gt, lt
  Comparator #(.width(7), .mode("unsigned")) comparator_2 (.a(Tag), .b(Tag1), .eq(E1));  // open: gt, lt
  Comparator #(.width(7), .mode("unsigned")) comparator_3 (.a(Tag), .b(Tag2), .eq(E2));  // open: gt, lt
  Line Line1 (
    .CLK(CLK), .Evict(Evict), .Selected(Select0), .CpuRead(CpuRead), .CpuWrite(CpuWrite),
    .CpuWriteValue(CpuWriteValue), .BlockSize(BlockSize), .NewTag(Tag), .LineFromMem(LineFromMem),
    .Valid(Valid0), .Dirty(Dirty0), .OutTag(Tag0), .ByteRead(ByteRead0), .MemRead(MemRead0),
    .MemWrite(MemWrite0), .Line2Mem(Line2Mem0));
  StageSwitcher stageswitcher_1 (
    .CLK(CLK), .Ready(Ready), .Stage1PrepareEvictSelect(Stage1), .Stag6UpdateAges(UpdateAge));  // open: Stage2WrtToMem, Stage3ReadFrmMem, Stage4WriteToCache, Stage5ReadfromCache
  // Probe on DidContain
  // Probe on ByteRead
  // Probe on Tag_2
  // Probe on MemRead
  // Probe on MemWrite
  // Probe on Line2Mem
  Multiplexer #(.width(2), .enable("false")) multiplexer_4 (
    .in0(Age0), .in1(NewAge0), .out(multiplexer_4_out), .sel(UpdateAge));
  Multiplexer #(.width(2), .enable("false")) multiplexer_5 (
    .in0(Age1), .in1(NewAge1), .out(multiplexer_5_out), .sel(UpdateAge));
  Multiplexer #(.width(2), .enable("false")) multiplexer_6 (
    .in0(Age2), .in1(NewAge2), .out(multiplexer_6_out), .sel(UpdateAge));
  Register #(.width(2)) State (.D(multiplexer_4_out), .en(ThisSet), .Q(Age0), .clk(CLK));  // open: clr
  Register #(.width(2)) State_2 (.D(multiplexer_5_out), .en(ThisSet), .Q(Age1), .clk(CLK));  // open: clr
  Register #(.width(2)) State_3 (.D(multiplexer_6_out), .en(ThisSet), .Q(Age2), .clk(CLK));  // open: clr
  SelectLine selectline_1 (
    .E0(E0), .E1(E1), .E2(E2), .Valid0(Valid0), .Valid1(Valid1), .Valid2(Valid2),
    .CheckAge(selectline_1_checkage), .Evict(selectline_1_evict), .ChooseBit1(selectline_1_choosebit0[1]),
    .ChooseBit0(selectline_1_choosebit0[0]));
  EvictDueToAge evictduetoage_1 (.Age0(Age0), .Age1(Age1), .Age2(Age2), .Select(evictduetoage_1_select));
  Line Line2 (
    .CLK(CLK), .Evict(Evict), .Selected(Select1), .CpuRead(CpuRead), .CpuWrite(CpuWrite),
    .CpuWriteValue(CpuWriteValue), .BlockSize(BlockSize), .NewTag(Tag), .LineFromMem(LineFromMem),
    .Valid(Valid1), .Dirty(Dirty1), .OutTag(Tag1), .ByteRead(ByteRead1), .MemRead(MemRead1),
    .MemWrite(MemWrite1), .Line2Mem(Line2Mem1));
  and and_4 (and_4_out, ThisSet, Stage1);
  Register #(.width(1)) State_4 (.D(selectline_1_evict), .en(and_4_out), .Q(Evict), .clk(CLK));  // open: clr
  // Probe on multiplexer_7_out
  Multiplexer #(.width(2), .enable("false")) multiplexer_7 (
    .in0(selectline_1_choosebit0), .in1(evictduetoage_1_select), .out(multiplexer_7_out),
    .sel(selectline_1_checkage));
  and and_5 (and_5_out, ThisSet, Stage1);
  AgeState agestate_1 (
    .Select(Select), .Age0(Age0), .Age1(Age1), .Age2(Age2), .Valid0(Valid0), .Valid1(Valid1),
    .Valid2(Valid2), .Age0p(NewAge0), .Age1p(NewAge1), .Age2p(NewAge2));
  Register #(.width(2)) State_5 (.D(multiplexer_7_out), .en(and_5_out), .Q(Select), .clk(CLK));  // open: clr
  and and_6 (and_6_out, E0, Valid0);
  and and_7 (and_7_out, E1, Valid1);
  and and_8 (and_8_out, E2, Valid2);
  Line Line3 (
    .CLK(CLK), .Evict(Evict), .Selected(Select2), .CpuRead(CpuRead), .CpuWrite(CpuWrite),
    .CpuWriteValue(CpuWriteValue), .BlockSize(BlockSize), .NewTag(Tag), .LineFromMem(LineFromMem),
    .Valid(Valid2), .Dirty(Dirty2), .OutTag(Tag2), .ByteRead(ByteRead2), .MemRead(MemRead2),
    .MemWrite(MemWrite2), .Line2Mem(Line2Mem2));
  or or_1 (or_1_out, and_6_out, and_7_out, and_8_out);
  Register #(.width(1)) State_6 (.D(or_1_out), .en(Stage1), .Q(DidContain), .clk(CLK));  // open: clr
  Multiplexer #(.select(2), .width(8), .enable("false")) multiplexer_8 (
    .in0(ByteRead0), .in1(ByteRead1), .in2(ByteRead2), .out(ByteRead), .sel(Select));  // open: in3
  Multiplexer #(.select(2), .width(7), .enable("false")) multiplexer_9 (
    .in0(Tag0), .in1(Tag1), .in2(Tag2), .out(Tag_2), .sel(Select));  // open: in3
  Multiplexer #(.select(2), .enable("false")) multiplexer_10 (
    .in0(MemRead0), .in1(MemRead1), .in2(MemRead2), .in3(1'b0), .out(MemRead), .sel(Select));
  Multiplexer #(.select(2), .enable("false")) multiplexer_11 (
    .in0(MemWrite0), .in1(MemWrite1), .in2(MemWrite2), .in3(1'b0), .out(MemWrite), .sel(Select));
  Multiplexer #(.select(2), .width(32), .enable("false")) multiplexer_12 (
    .in0(Line2Mem0), .in1(Line2Mem1), .in2(Line2Mem2), .out(Line2Mem), .sel(Select));  // open: in3

  // Other names for the same wires on the sheet: InTag[6:0] = Tag; Tag_t[6:0] = Tag_2

  // Notes on the sheet:
  //   !!Note:Valid here should be after update
endmodule

module Line (
  input  CLK,
  input  Evict,
  input  Selected,
  input  CpuRead,
  input  CpuWrite,
  input  [7:0] CpuWriteValue,
  input  [1:0] BlockSize,
  input  [6:0] NewTag,
  input  [31:0] LineFromMem,
  output Valid,
  output Dirty,
  output [6:0] OutTag,
  output [7:0] ByteRead,
  output MemRead,
  output MemWrite,
  output [31:0] Line2Mem
);

  wire and_1_out, comparator_1_eq, comparator_2_eq, comparator_3_eq, comparator_4_eq, multiplexer_5_out,
       multiplexer_6_out, multiplexer_8_out, S4CpuWrite, Stage2, Stage3, Stage4;
  wire [6:0] multiplexer_10_out, OutTag_t;
  wire [7:0] bitselector_1_out;
  wire [31:0] multiplexer_7_out, multiplexer_9_out, NewCacheValue;

  StageSwitcher stageswitcher_1 (
    .CLK(CLK), .Stage2WrtToMem(Stage2), .Stage3ReadFrmMem(Stage3), .Stage4WriteToCache(Stage4));  // open: Ready, Stage1PrepareEvictSelect, Stage5ReadfromCache, Stag6UpdateAges
  and and_1 (and_1_out, Valid, Dirty, Evict);
  Comparator #(.width(2), .mode("unsigned")) comparator_1 (
    .a(BlockSize), .b(2'b00), .eq(comparator_1_eq));  // open: gt, lt
  Comparator #(.width(2), .mode("unsigned")) comparator_2 (
    .a(BlockSize), .b(2'b01), .eq(comparator_2_eq));  // open: gt, lt
  Comparator #(.width(2), .mode("unsigned")) comparator_3 (
    .a(BlockSize), .b(2'b10), .eq(comparator_3_eq));  // open: gt, lt
  Comparator #(.width(2), .mode("unsigned")) comparator_4 (
    .a(BlockSize), .b(2'b11), .eq(comparator_4_eq));  // open: gt, lt
  and and_2 (MemRead, Evict, Stage3);
  and and_3 (S4CpuWrite, Stage4, CpuWrite);
  and and_4 (MemWrite, and_1_out, Stage2);
  Multiplexer #(.width(8), .enable("false")) multiplexer_1 (
    .in0(Line2Mem[7:0]), .in1(CpuWriteValue), .out(NewCacheValue[7:0]), .sel(comparator_1_eq));
  Multiplexer #(.width(8), .enable("false")) multiplexer_2 (
    .in0(Line2Mem[15:8]), .in1(CpuWriteValue), .out(NewCacheValue[15:8]), .sel(comparator_2_eq));
  Multiplexer #(.width(8), .enable("false")) multiplexer_3 (
    .in0(Line2Mem[23:16]), .in1(CpuWriteValue), .out(NewCacheValue[23:16]), .sel(comparator_3_eq));
  Multiplexer #(.width(8), .enable("false")) multiplexer_4 (
    .in0(Line2Mem[31:24]), .in1(CpuWriteValue), .out(NewCacheValue[31:24]), .sel(comparator_4_eq));
  Multiplexer #(.enable("false")) multiplexer_5 (.in0(Valid), .in1(1'b1), .out(multiplexer_5_out), .sel(MemRead));
  Multiplexer #(.enable("false")) multiplexer_6 (.in0(Dirty), .in1(1'b0), .out(multiplexer_6_out), .sel(MemWrite));
  Register #(.width(1)) State (.D(multiplexer_5_out), .en(Selected), .Q(Valid), .clk(CLK));  // open: clr
  Multiplexer #(.width(32), .enable("false")) multiplexer_7 (
    .in0(Line2Mem), .in1(LineFromMem), .out(multiplexer_7_out), .sel(MemRead));
  Multiplexer #(.enable("false")) multiplexer_8 (
    .in0(multiplexer_6_out), .in1(1'b1), .out(multiplexer_8_out), .sel(S4CpuWrite));
  Multiplexer #(.width(32), .enable("false")) multiplexer_9 (
    .in0(multiplexer_7_out), .in1(NewCacheValue), .out(multiplexer_9_out), .sel(S4CpuWrite));
  Register #(.width(1)) State_2 (.D(multiplexer_8_out), .en(Selected), .Q(Dirty), .clk(CLK));  // open: clr
  // Probe on multiplexer_9_out
  Multiplexer #(.width(7), .enable("false")) multiplexer_10 (
    .in0(OutTag_t), .in1(NewTag), .out(multiplexer_10_out), .sel(MemRead));
  Register #(.width(32)) State_3 (.D(multiplexer_9_out), .en(Selected), .Q(Line2Mem), .clk(CLK));  // open: clr
  // Probe on OutTag_t
  Register #(.width(7)) State_4 (.D(multiplexer_10_out), .en(Selected), .Q(OutTag_t), .clk(CLK));  // open: clr
  // Probe on Line2Mem
  BitSelector #(.width(32), .group(8)) bitselector_1 (.in(Line2Mem), .out(bitselector_1_out), .sel(BlockSize));
  Multiplexer #(.width(8), .enable("false")) multiplexer_11 (
    .in0(bitselector_1_out), .in1(CpuWriteValue), .out(ByteRead), .sel(S4CpuWrite));
  Multiplexer #(.width(7), .enable("false")) multiplexer_12 (.in0(OutTag_t), .in1(NewTag), .out(OutTag), .sel(MemRead));

  // Other names for the same wires on the sheet: Byte0[7:0] = Line2Mem[7:0]; Byte1[7:0] = Line2Mem[15:8];
  //   Byte2[7:0] = Line2Mem[23:16]; Byte3[7:0] = Line2Mem[31:24]; S2MemWrite = MemWrite; S3MemRead = MemRead

  // Notes on the sheet:
  //   Write to memory
  //   Read from Memory
  //   Read from Cache
  //   Write to Cache and set Dirty
endmodule

module SelectLine (
  input  E0,
  input  E1,
  input  E2,
  input  Valid0,
  input  Valid1,
  input  Valid2,
  output CheckAge,
  output Evict,
  output ChooseBit1,
  output ChooseBit0
);

  wire and_2_out, and_3_out, and_4_out, and_5_out, and_6_out, and_7_out, and_8_out, and_9_out, not_1_out,
       not_2_out, not_3_out, not_4_out, not_5_out, not_6_out, not_7_out, not_8_out, not_9_out, not_10_out,
       not_11_out, not_12_out, not_13_out, not_14_out, not_15_out, not_16_out, not_17_out, not_18_out,
       not_19_out, not_20_out;

  not not_1 (not_1_out, E0);
  not not_2 (not_2_out, E1);
  not not_3 (not_3_out, E2);
  not not_4 (not_4_out, E0);
  not not_5 (not_5_out, E1);
  not not_6 (not_6_out, E2);
  not not_7 (not_7_out, E0);
  not not_8 (not_8_out, E1);
  not not_9 (not_9_out, Valid2);
  not not_10 (not_10_out, E0);
  not not_11 (not_11_out, Valid1);
  not not_12 (not_12_out, Valid0);
  not not_13 (not_13_out, E0);
  not not_14 (not_14_out, E1);
  not not_15 (not_15_out, E0);
  not not_16 (not_16_out, E1);
  not not_17 (not_17_out, E0);
  not not_18 (not_18_out, E2);
  not not_19 (not_19_out, Valid1);
  not not_20 (not_20_out, E0);
  and and_1 (CheckAge, not_1_out, not_2_out, not_3_out, Valid0, Valid1, Valid2);
  and and_2 (and_2_out, not_4_out, not_5_out, not_6_out);
  and and_3 (and_3_out, not_7_out, not_8_out, not_9_out);
  and and_4 (and_4_out, not_10_out, E1, not_11_out);
  and and_5 (and_5_out, E0, not_12_out);
  and and_6 (and_6_out, not_13_out, not_14_out, Valid0, Valid1);
  and and_7 (and_7_out, not_15_out, not_16_out, E2);
  and and_8 (and_8_out, not_17_out, not_18_out, Valid0, not_19_out);
  and and_9 (and_9_out, not_20_out, E1);
  or or_1 (Evict, and_2_out, and_3_out, and_4_out, and_5_out);
  or or_2 (ChooseBit1, and_6_out, and_7_out);
  or or_3 (ChooseBit0, and_8_out, and_9_out);
endmodule

module EvictDueToAge (
  input  [1:0] Age0,
  input  [1:0] Age1,
  input  [1:0] Age2,
  output [1:0] Select
);

  wire comparator_1_lt, comparator_2_gt, comparator_3_gt;
  wire [1:0] multiplexer_1_out, multiplexer_2_out;

  Comparator #(.width(2), .mode("unsigned")) comparator_1 (.a(Age0), .b(Age1), .lt(comparator_1_lt));  // open: gt, eq
  Comparator #(.width(2), .mode("unsigned")) comparator_2 (.a(Age0), .b(Age2), .gt(comparator_2_gt));  // open: eq, lt
  Comparator #(.width(2), .mode("unsigned")) comparator_3 (.a(Age1), .b(Age2), .gt(comparator_3_gt));  // open: eq, lt
  Multiplexer #(.width(2), .enable("false")) multiplexer_1 (
    .in0(2'b10), .in1(2'b00), .out(multiplexer_1_out), .sel(comparator_2_gt));
  Multiplexer #(.width(2), .enable("false")) multiplexer_2 (
    .in0(2'b10), .in1(2'b01), .out(multiplexer_2_out), .sel(comparator_3_gt));
  Multiplexer #(.width(2), .enable("false")) multiplexer_3 (
    .in0(multiplexer_1_out), .in1(multiplexer_2_out), .out(Select), .sel(comparator_1_lt));
endmodule

module AgeState (
  input  [1:0] Select,
  input  [1:0] Age0,
  input  [1:0] Age1,
  input  [1:0] Age2,
  input  Valid0,
  input  Valid1,
  input  Valid2,
  output [1:0] Age0p,
  output [1:0] Age1p,
  output [1:0] Age2p
);

  wire and_1_out, and_3_out, and_4_out, and_5_out, comparator_1_eq, comparator_2_eq, comparator_3_eq,
       not_1_out, or_1_out, Safe;
  wire [1:0] adder_1_out, adder_2_out, adder_3_out, Age0s1, Age1s1, Age2s1, Comparator, multiplexer_5_out,
       multiplexer_6_out, multiplexer_7_out, multiplexer_8_out, multiplexer_9_out, multiplexer_10_out,
       multiplexer_11_out, multiplexer_12_out, multiplexer_13_out;
  wire [2:0] comparator_4_gt, comparator_5_gt, comparator_6_gt;

  // Probe on Age0p
  // Probe on Age1p
  // Probe on Age2p
  Multiplexer #(.width(2), .enable("false")) multiplexer_1 (.in0(2'b00), .in1(Age0), .out(Age0s1), .sel(Valid0));
  Multiplexer #(.width(2), .enable("false")) multiplexer_2 (.in0(2'b00), .in1(Age1), .out(Age1s1), .sel(Valid1));
  Multiplexer #(.width(2), .enable("false")) multiplexer_3 (.in0(2'b00), .in1(Age2), .out(Age2s1), .sel(Valid2));
  Comparator #(.width(2), .mode("unsigned")) comparator_1 (
    .a(Age0s1), .b(2'b10), .eq(comparator_1_eq));  // open: gt, lt
  Comparator #(.width(2), .mode("unsigned")) comparator_2 (
    .a(Age1s1), .b(2'b10), .eq(comparator_2_eq));  // open: gt, lt
  Comparator #(.width(2), .mode("unsigned")) comparator_3 (
    .a(Age2s1), .b(2'b10), .eq(comparator_3_eq));  // open: gt, lt
  Multiplexer #(.select(2), .width(2), .enable("false")) multiplexer_4 (
    .in0(Age0s1), .in1(Age1s1), .in2(Age2s1), .out(Comparator), .sel(Select));  // open: in3
  or or_1 (or_1_out, comparator_1_eq, comparator_2_eq, comparator_3_eq);
  and and_1 (and_1_out, Valid0, Valid1, Valid2);
  not not_1 (not_1_out, or_1_out);
  and and_2 (Safe, not_1_out, and_1_out);
  and and_3 (and_3_out, Safe, comparator_4_gt[0]);
  Multiplexer #(.width(2), .enable("false")) multiplexer_5 (
    .in0(Age0s1), .in1(adder_1_out), .out(multiplexer_5_out), .sel(and_3_out));
  Adder #(.width(2)) adder_1 (.a(Age0s1), .b(2'b01), .out(adder_1_out));  // open: cin, cout
  Adder #(.width(2)) adder_2 (.a(Age1s1), .b(2'b01), .out(adder_2_out));  // open: cin, cout
  Adder #(.width(2)) adder_3 (.a(Age2s1), .b(2'b01), .out(adder_3_out));  // open: cin, cout
  and and_4 (and_4_out, Safe, comparator_5_gt[0]);
  Multiplexer #(.width(2), .enable("false")) multiplexer_6 (
    .in0(Age1s1), .in1(adder_2_out), .out(multiplexer_6_out), .sel(and_4_out));
  and and_5 (and_5_out, Safe, comparator_6_gt[0]);
  Multiplexer #(.width(2), .enable("false")) multiplexer_7 (
    .in0(Age2s1), .in1(adder_3_out), .out(multiplexer_7_out), .sel(and_5_out));
  Comparator #(.width(2), .mode("unsigned")) comparator_4 (
    .a(Age0s1), .b(Comparator), .gt(comparator_4_gt[0]), .eq(comparator_4_gt[1]), .lt(comparator_4_gt[2]));
  Comparator #(.width(2), .mode("unsigned")) comparator_5 (
    .a(Age1s1), .b(Comparator), .gt(comparator_5_gt[0]), .eq(comparator_5_gt[1]), .lt(comparator_5_gt[2]));
  Comparator #(.width(2), .mode("unsigned")) comparator_6 (
    .a(Age2s1), .b(Comparator), .gt(comparator_6_gt[0]), .eq(comparator_6_gt[1]), .lt(comparator_6_gt[2]));
  Multiplexer #(.select(3), .width(2), .enable("false")) multiplexer_8 (
    .in1(multiplexer_5_out), .in2(adder_1_out), .in4(adder_1_out), .out(multiplexer_8_out),
    .sel(comparator_4_gt));  // open: in0, in3, in5, in6, in7
  Multiplexer #(.select(3), .width(2), .enable("false")) multiplexer_9 (
    .in1(multiplexer_6_out), .in2(adder_2_out), .in4(adder_2_out), .out(multiplexer_9_out),
    .sel(comparator_5_gt));  // open: in0, in3, in5, in6, in7
  Multiplexer #(.select(3), .width(2), .enable("false")) multiplexer_10 (
    .in1(multiplexer_7_out), .in2(adder_3_out), .in4(adder_3_out), .out(multiplexer_10_out),
    .sel(comparator_6_gt));  // open: in0, in3, in5, in6, in7
  Multiplexer #(.width(2), .enable("false")) multiplexer_11 (
    .in0(2'b00), .in1(multiplexer_8_out), .out(multiplexer_11_out), .sel(Valid0));
  Multiplexer #(.width(2), .enable("false")) multiplexer_12 (
    .in0(2'b00), .in1(multiplexer_9_out), .out(multiplexer_12_out), .sel(Valid1));
  Multiplexer #(.width(2), .enable("false")) multiplexer_13 (
    .in0(2'b00), .in1(multiplexer_10_out), .out(multiplexer_13_out), .sel(Valid2));
  Multiplexer #(.select(2), .width(2), .enable("false")) multiplexer_14 (
    .in0(2'b00), .in1(multiplexer_11_out), .in2(multiplexer_11_out), .in3(multiplexer_11_out), .out(Age0p),
    .sel(Select));
  Multiplexer #(.select(2), .width(2), .enable("false")) multiplexer_15 (
    .in0(multiplexer_13_out), .in1(multiplexer_13_out), .in2(2'b00), .in3(multiplexer_13_out), .out(Age2p),
    .sel(Select));
  Multiplexer #(.select(2), .width(2), .enable("false")) multiplexer_16 (
    .in0(multiplexer_12_out), .in1(2'b00), .in2(multiplexer_12_out), .in3(multiplexer_12_out), .out(Age1p),
    .sel(Select));

  // Other names for the same wires on the sheet: _0[1:0] = Age0p; _1[1:0] = Age1p; _2[1:0] = Age2p
endmodule

// Stages
module StageSwitcher (
  input  CLK,
  output Ready,
  output Stage1PrepareEvictSelect,
  output Stage2WrtToMem,
  output Stage3ReadFrmMem,
  output Stage4WriteToCache,
  output Stage5ReadfromCache,
  output Stag6UpdateAges
);

  wire [3:0] Counter;

  Counter #(.width(4), .max('h6)) HitCounter (.D(4'b0000), .Q(Counter), .clk(CLK));  // open: load, count, carry, clr
  Comparator #(.width(4), .mode("unsigned")) comparator_1 (.a(Counter), .b(4'b0000), .eq(Ready));  // open: gt, lt
  Comparator #(.width(4), .mode("unsigned")) comparator_2 (
    .a(Counter), .b(4'b0001), .eq(Stage1PrepareEvictSelect));  // open: gt, lt
  Comparator #(.width(4), .mode("unsigned")) comparator_3 (
    .a(Counter), .b(4'b0010), .eq(Stage2WrtToMem));  // open: gt, lt
  Comparator #(.width(4), .mode("unsigned")) comparator_4 (
    .a(Counter), .b(4'b0011), .eq(Stage3ReadFrmMem));  // open: gt, lt
  Comparator #(.width(4), .mode("unsigned")) comparator_5 (
    .a(Counter), .b(4'b0100), .eq(Stage4WriteToCache));  // open: gt, lt
  Comparator #(.width(4), .mode("unsigned")) comparator_6 (
    .a(Counter), .b(4'b0101), .eq(Stage5ReadfromCache));  // open: gt, lt
  Comparator #(.width(4), .mode("unsigned")) comparator_7 (
    .a(Counter), .b(4'b0110), .eq(Stag6UpdateAges));  // open: gt, lt

  // Other names for the same wires on the sheet: Stage0 = Ready; Stage1 = Stage1PrepareEvictSelect;
  //   Stage2 = Stage2WrtToMem; Stage3 = Stage3ReadFrmMem; Stage4 = Stage4WriteToCache; Stage5 = Stage5ReadfromCache;
  //   Stage6 = Stag6UpdateAges

  // Notes on the sheet:
  //   Write to memory
  //   Read from Memory
  //   Write to Cache and set Dirty
  //   Read from Cache
  //   UpdateAge
endmodule

module Inputs (
  input  HaltTesting,
  input  Ready,
  input  CLK,
  output Done,
  output Read,
  output Write,
  output [9:0] Address,
  output [7:0] Value,
  output [9:0] TestNumber
);

  wire and_1_out, not_1_out, not_2_out;

  not not_1 (not_1_out, HaltTesting);
  not not_2 (not_2_out, Done);
  Counter #(.width(10), .max('h3ff), .ongoal("stay")) u_TestNumber (
    .count(and_1_out), .Q(TestNumber), .clk(CLK));  // open: load, D, carry, clr
  and and_1 (and_1_out, not_1_out, Ready, not_2_out);
  ROM #(.addrWidth(10), .dataWidth(21)) rom_1 (
    .addr(TestNumber), .data({Done, Read, Write, Address, Value}));  // open: sel

  // Notes on the sheet:
  //   contents of rom_1 (hex, n*v repeats v):
  //   80882 83fe6 4306b 83e0e 43701 42275 8280f 80304 41bd8 84371 43f77 41d70 4250b 44733 8253d 440d8
  //   82691 440c9 83d7c 43558 446bf 83837 842c9 43e0f 4059d 41556 80166 833b0 43a89 83142 8361c 42e66
  //   43eb6 42c00 43a0e 8165c 84682 8092a 83907 41f89 817b0 40855 82056 425e8 43ff2 8039f 42bd7 82137
  //   4416b 40273 8324a 814e4 44570 41c0f 429da 82640 8069c 8099e 414d5 41004 81beb 84113 419b1 81add
  //   83f35 425ff 829cd 40250 82945 4366d 40cc2 444f8 80814 81156 8446d 42a82 42bae 82578 41135 405d0
  //   8304b 82b3a 40972 822ba 4443a 42337 82506 80bd3 80560 83552 83955 81434 43096 43da1 81aa2 80305
  //   428e6 428cc 808a2 40e80 845f0 4215d 82765 82e29 40be5 82b74 42715 417a2 41fab 8452f 81c0a 83325
  //   44624 80205 42dfc 41333 40958 81348 42736 41069 84510 44669 826dd 8067e 408e4 44680 444e8 832ad
  //   821f8 83509 82d46 81184 432cd 80b77 4005a 440e0 81ea0 43d73 42b8c 80624 41468 42699 415ed 80fc1 0
  //   100000
endmodule

module Checker (
  input  [9:0] TestNumber,
  input  [7:0] YourByteRead,
  output CmdIsRead,
  output [7:0] CorrectByteRead,
  output Correct
);

  wire comparator_1_eq;
  wire [9:0] subtractor_1_out;

  // Probe on TestNumber
  Subtractor #(.width(10)) subtractor_1 (.a(TestNumber), .b(10'h1), .out(subtractor_1_out));  // open: bin, bout
  ROM #(.addrWidth(10), .dataWidth(9)) rom_1 (
    .addr(subtractor_1_out), .data({CmdIsRead, CorrectByteRead}));  // open: sel
  Comparator #(.mode("unsigned")) comparator_1 (
    .a(YourByteRead), .b(CorrectByteRead), .eq(comparator_1_eq));  // open: gt, lt
  and and_1 (Correct, comparator_1_eq, CmdIsRead);

  // Other names for the same wires on the sheet: Test_Number[9:0] = TestNumber

  // Notes on the sheet:
  //   Read Solutions
  //   contents of rom_1 (hex, n*v repeats v):
  //   1a3 1dc 6b 125 1 75 1dc 1c3 d8 1ab 77 70 b 33 10b d8 1c3 c9 174 58 bf 153 199 f 9d 56 1bb 13b 89 16c
  //   180 66 b6 0 e 107 1bf 1d8 167 89 118 55 1a2 e8 f2 1c3 d7 142 6b 73 1ab 18c 70 f da 1c3 14c 1d8 d5 4
  //   1d8 16b b1 1f4 1f2 ff 1da 50 1da 6d c2 f8 155 1c6 1f8 82 ae 1ff 35 d0 16b 1ae 72 175 3a 37 1ff 173
  //   1d0 158 167 1d5 96 a1 1f4 1c3 e6 cc 155 80 170 5d 1e6 166 e5 1ae 15 a2 ab 170 10f 13b 24 150 fc 33
  //   58 133 36 69 170 69 1c3 14c e4 80 e8 1ab 15d 158 1fc 135 cd 1e5 5a e0 104 73 8c 14c 68 99 ed 1a6
endmodule

module CheckTagValid (
  input  Eq0,
  input  Eq1,
  input  Eq2,
  input  Valid0,
  input  Valid1,
  input  Valid2,
  output CheckAge,
  output Evict,
  output Valid0_2,
  output Valid1_2,
  output Valid2_2,
  output ChooseBit1,
  output ChooseBit0
);

  wire and_2_out, and_3_out, and_4_out, and_5_out, and_6_out, and_7_out, and_8_out, and_9_out, and_10_out,
       not_1_out, not_2_out, not_3_out, not_4_out, not_5_out, not_6_out, not_7_out, not_8_out, not_9_out,
       not_10_out, not_11_out, not_12_out, not_13_out, not_14_out, not_15_out, not_16_out, not_17_out,
       not_18_out, not_19_out, not_20_out;

  not not_1 (not_1_out, Eq0);
  not not_2 (not_2_out, Eq1);
  not not_3 (not_3_out, Eq2);
  not not_4 (not_4_out, Eq0);
  not not_5 (not_5_out, Eq1);
  not not_6 (not_6_out, Eq2);
  not not_7 (not_7_out, Valid2);
  not not_8 (not_8_out, Valid1);
  not not_9 (not_9_out, Valid0);
  not not_10 (not_10_out, Eq1);
  not not_11 (not_11_out, Eq2);
  not not_12 (not_12_out, Eq0);
  not not_13 (not_13_out, Eq2);
  not not_14 (not_14_out, Eq0);
  not not_15 (not_15_out, Eq1);
  not not_16 (not_16_out, Eq0);
  not not_17 (not_17_out, Eq1);
  not not_18 (not_18_out, Eq0);
  not not_19 (not_19_out, Eq2);
  not not_20 (not_20_out, Valid1);
  and and_1 (CheckAge, not_1_out, not_2_out, not_3_out, Valid0, Valid1, Valid2);
  and and_2 (and_2_out, not_4_out, not_5_out, not_6_out);
  and and_3 (and_3_out, Eq2, not_7_out);
  and and_4 (and_4_out, Eq1, not_8_out);
  and and_5 (and_5_out, Eq0, not_9_out);
  and and_6 (and_6_out, not_10_out, not_11_out);
  and and_7 (and_7_out, not_12_out, not_13_out, Valid0);
  and and_8 (and_8_out, not_14_out, not_15_out, Valid0, Valid1);
  and and_9 (and_9_out, not_16_out, not_17_out, Valid0, Valid1);
  and and_10 (and_10_out, not_18_out, not_19_out, Valid0, not_20_out);
  or or_1 (Evict, and_2_out, and_3_out, and_4_out, and_5_out);
  or or_2 (Valid0_2, and_6_out, Valid0);
  or or_3 (Valid1_2, Valid1, and_7_out, Eq1);
  or or_4 (Valid2_2, Valid2, and_8_out, Eq2);
  or or_5 (ChooseBit1, and_9_out, Eq2);
  or or_6 (ChooseBit0, and_10_out, Eq1);
endmodule
